// Logisim project Weird_CPU_v1.circ as structural Verilog: 1 circuit, main circuit Weird_CPU
module Weird_CPU (
);

  wire A_WR, adder_1_cout, ADDR_SEL, and_2_out, and_3_out, and_4_out, and_5_out, and_6_out, and_7_out,
       and_8_out, and_9_out, and_10_out, and_15_out, CLK, CLK_STOP, clock_1_out, comparator_1_eq,
       comparator_2_eq, comparator_3_eq, comparator_4_eq, Cout, DATAMEM, demultiplexer_1_out0,
       demultiplexer_1_out1, demultiplexer_2_out0, demultiplexer_2_out1, IOMEM, JUMP_CYCLE, MEM_READ,
       MEM_WRITE, MWR, not_2_out, not_3_out, not_4_out, or_1_out, P_JMP, P_UPDATE, RD_EA, RD_I, RST;
  wire [1:0] ALU_MUX, CTR_q;
  wire [3:0] register_1_q, register_1_q_2;
  wire [6:0] keyboard_1_data;
  wire [7:0] A_q, adder_1_out, DATA, I, MICROCODE_data, multiplexer_1_out, multiplexer_2_out,
       multiplexer_5_out, multiplexer_7_out, nand_1_out, not_1_out, P_q, PCH, UADDR;
  wire [7:7] keyboard_1_avail;
  wire [15:0] adder_2_out, ADDR, E_q, multiplexer_3_out, multiplexer_4_out;

  Button button_1 (.out(RST));
  and and_1 (CLK, CLK_STOP, clock_1_out);
  Clock clock_1 (.out(clock_1_out));
  Counter #(.max('h3), .width(2)) CTR (
    .clr(RST), .load(1'b0), .up(1'b1), .count(1'b1), .clk(CLK), .Q(CTR_q));  // open: D, carry
  Comparator #(.mode("unsigned")) comparator_1 (.a(ADDR[7:0]), .b(8'hfd), .eq(comparator_1_eq));  // open: gt, lt
  and and_2 (and_2_out, I[1], JUMP_CYCLE);
  and and_3 (and_3_out, I[6], ~JUMP_CYCLE);  // AND_Gate
  and and_4 (and_4_out, MWR, IOMEM, comparator_1_eq);
  Register u_I (.D(DATA), .en(RD_I), .clk(CLK), .Q({I[7:4], ALU_MUX, I[1:0]}), .clr(RST));
  Multiplexer #(.width(8)) multiplexer_1 (.in0(PCH), .in1(UADDR), .out(multiplexer_1_out), .sel(and_2_out));
  Multiplexer #(.width(8)) multiplexer_2 (
    .in0(multiplexer_1_out), .in1({8{1'b0}}), .out(multiplexer_2_out), .sel(and_3_out));
  Register register_1 (.D(DATA), .en(and_4_out), .clk(CLK), .Q({register_1_q_2, register_1_q}), .clr(RST));
  assign not_1_out = ~DATA;  // NOT_Gate not_1, 8 bits wide
  Multiplexer #(.width(16)) multiplexer_3 (
    .in0(E_q), .in1({multiplexer_2_out, DATA}), .out(multiplexer_3_out), .sel(I[1]));
  Decoder #(.enable("false"), .select(2)) decoder_1 (.out2(JUMP_CYCLE), .sel(CTR_q));  // open: out0, out1, out3
  ROM #(.addrWidth(2)) MICROCODE (
    .addr(CTR_q), .data({MICROCODE_data[7], RD_I, MICROCODE_data[5], ADDR_SEL, P_UPDATE, MICROCODE_data[2:0]}));
  Hex_Digit_Display hex_digit_display_1 (.value(register_1_q_2));  // open: dp
  Hex_Digit_Display hex_digit_display_2 (.value(register_1_q));  // open: dp
  Adder adder_1 (.a(A_q), .b(DATA), .out(adder_1_out), .cin(1'b0), .cout(adder_1_cout));
  assign nand_1_out = ~(DATA & A_q);  // NAND_Gate nand_1, 8 bits wide
  Adder #(.width(16)) adder_2 (.a({PCH, P_q}), .b(16'h1), .out(adder_2_out), .cin(1'b0));  // open: cout
  Register #(.width(16)) E (.D({multiplexer_2_out, DATA}), .en(RD_EA), .clk(CLK), .Q(E_q), .clr(RST));
  Register #(.width(16)) P (.D(multiplexer_4_out), .en(P_UPDATE), .clk(CLK), .Q({PCH, P_q}), .clr(RST));
  Multiplexer #(.width(16)) multiplexer_4 (
    .in0(adder_2_out), .in1(multiplexer_3_out), .out(multiplexer_4_out), .sel(P_JMP));
  Multiplexer #(.select(2), .width(8)) multiplexer_5 (
    .in0(DATA), .in1(adder_1_out), .in2(nand_1_out), .in3(not_1_out), .out(multiplexer_5_out), .sel(ALU_MUX));
  Demultiplexer demultiplexer_1 (.out0(demultiplexer_1_out0), .out1(demultiplexer_1_out1), .in(A_WR), .sel(I[4]));
  Multiplexer #(.width(16)) multiplexer_6 (.in0(E_q), .in1({PCH, P_q}), .out(ADDR), .sel(ADDR_SEL));
  and and_5 (and_5_out, MWR, IOMEM, comparator_2_eq);
  Comparator #(.mode("unsigned")) comparator_2 (.a(ADDR[7:0]), .b({8{1'b1}}), .eq(comparator_2_eq));  // open: gt, lt
  Register U (.D(multiplexer_5_out), .en(demultiplexer_1_out1), .clk(CLK), .Q(UADDR), .clr(RST));
  Register A (.D(multiplexer_5_out), .en(demultiplexer_1_out0), .clk(CLK), .Q(A_q), .clr(RST));
  not not_2 (not_2_out, I[5]);
  Decoder decoder_2 (.out0(MEM_READ), .out1(MEM_WRITE), .sel(I[0]), .en(not_2_out));
  not not_3 (not_3_out, MWR);
  Comparator #(.mode("unsigned")) comparator_3 (.a(ADDR[7:0]), .b(8'hfe), .eq(comparator_3_eq));  // open: gt, lt
  or or_1 (or_1_out, I[4], ~Cout);  // OR_Gate
  TTY tty_1 (.data(DATA[6:0]), .clk(CLK), .we(and_5_out), .clr(and_6_out));
  and and_6 (and_6_out, and_5_out, DATA[7]);
  Keyboard keyboard_1 (.clk(CLK), .re(and_7_out), .avail(keyboard_1_avail[7]), .data(keyboard_1_data));  // open: clr
  and and_7 (and_7_out, not_3_out, A_WR, IOMEM, comparator_3_eq);
  Register #(.width(1)) C (.D(adder_1_cout), .en(demultiplexer_1_out0), .clk(CLK), .Q(Cout), .clr(RST));
  Demultiplexer demultiplexer_2 (
    .out0(demultiplexer_2_out0), .out1(demultiplexer_2_out1), .in(DATAMEM), .sel(not_4_out));
  assign DATA = MWR ? multiplexer_7_out : 8'bz;  // Controlled_Buffer controlled_buffer_1
  Multiplexer #(.width(8)) multiplexer_7 (.in0(A_q), .in1(UADDR), .out(multiplexer_7_out), .sel(I[4]));
  RAM #(.addrWidth(16), .asyncread("true"), .databus("bidir"), .\type ("nonvolatile")) MEM (
    .addr(ADDR), .we(demultiplexer_2_out0), .oe(demultiplexer_2_out1), .clk(CLK), .data(DATA));
  not not_4 (not_4_out, MWR);
  assign DATA = and_7_out ? {keyboard_1_avail[7], keyboard_1_data} : 8'bz;  // Controlled_Buffer controlled_buffer_2
  and and_8 (and_8_out, I[7], MICROCODE_data[7]);
  Decoder #(.enable("false")) decoder_3 (.out0(DATAMEM), .out1(IOMEM), .sel(and_8_out));
  and and_9 (and_9_out, JUMP_CYCLE, ~I[1]);  // AND_Gate
  and and_10 (and_10_out, MICROCODE_data[2], I[5]);
  and and_11 (P_JMP, and_10_out, or_1_out);
  and and_12 (A_WR, MICROCODE_data[1], MEM_READ);
  and and_13 (MWR, MICROCODE_data[0], MEM_WRITE);
  and and_14 (RD_EA, MICROCODE_data[5], ~and_9_out);  // AND_Gate
  Comparator #(.mode("unsigned")) comparator_4 (.a(ADDR[7:0]), .b({8{1'b0}}), .eq(comparator_4_eq));  // open: gt, lt
  Pull_Resistor #(.pull(1)) pull_resistor_1 (.node(DATA));
  and and_15 (and_15_out, MWR, IOMEM, comparator_4_eq);
  T_Flip_Flop t_ff_1 (.T(and_15_out), .clk(CLK), .Qn(CLK_STOP), .reset(RST));  // open: Q, preset

  // Other names for the same wires on the sheet: IOADDR[7:0] = ADDR[7:0]; I[3:2] = ALU_MUX; INDIRECT = I[1];
  //   JMP_UNCONDITIONAL = I[4]; RD_U = I[4]; JMP_ENABLE = I[5]; ZERO_PAGE = I[6]; IO_SW = I[7]

  // Notes on the sheet:
  //   contents of MICROCODE (hex, n*v repeats v):
  //   58 30 2c 83
  //   ALU & Register Datapath
  //   Simple I/O Devices
  //   Control Signal Generator / State Machine
  //   Main Memory
endmodule
